# Fritzing sketch circuit (saved by Fritzing 0.9.3b)

parts:
  Mod1 = Raspberry Pi Pico
  S2 = Pushbutton [package="[SMD]"]
  LED1 = smd LED [color="Blue (470nm)" package="0805 [SMD]"]
  LED2 = smd LED [color="Blue (470nm)" package="0805 [SMD]"]
  LED3 = smd LED [color="Blue (470nm)" package="0805 [SMD]"]
  LED4 = smd LED [color="Blue (470nm)" package="0805 [SMD]"]
  J1 = Piezo Speaker
  KF-1 = KF-301 Relay [package=THT]

nets:
  N1: Mod1.pin_3, Mod1.pin_13, Mod1.pin_18, Mod1.pin_42, S2.Pin_3, S2.Pin_4, LED1.cathode, LED2.cathode, LED3.cathode, LED4.cathode, KF-1.ground
  N2: Mod1.pin_4, LED4.anode
  N3: Mod1.pin_5, LED2.anode
  N4: Mod1.pin_6, LED1.anode
  N5: Mod1.pin_7, LED3.anode
  N6: Mod1.pin_15, S2.Pin_2
  N7: Mod1.pin_24, J1.pin2
  N8: Mod1.pin_26, KF-1.signal
  N9: Mod1.pin_39, KF-1.power

custom parts:
  Raspberry Pi Pico: Raspberry Pi Pico. Based around the RP2040 microcontroller the Pico is a low cost microcontroller device bringing Raspberry Pi quality, cost, and easy of use to the microcontroller space. Jan 2021, Split part in to two versions: tht (this one) and SMD. This one will drill holes for a .1 in header in pcb to allow plugging in the module as well as providing pads to solder the module to the top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
  KF-301 Relay: KF-301
